# Fritzing sketch cambio sentido motor PCB (saved by Fritzing 0.9.3b)
circuit board: 4.44202cm x 2.52165cm

parts:
  2N3904 = NPN-Transistor [package="TO92 [THT]"]
  2N3904_2 = NPN-Transistor [package="TO92 [THT]"]
  2N3904_3 = NPN-Transistor [package="TO92 [THT]"]
  2N3904_4 = NPN-Transistor [package="TO92 [THT]"]
  1N4007 = Rectifier Diode [part_number=1N4001 package="300 mil [THT]"]
  1N4007_2 = Rectifier Diode [part_number=1N4007 package="300 mil [THT]"]
  1N4007_3 = Rectifier Diode [part_number=1N4001 package="300 mil [THT]"]
  1N4007_4 = Rectifier Diode [part_number=1N4001 package="300 mil [THT]"]
  1k = Resistor [tolerance=±5% resistance=220 package=THT]
  1K = Resistor [tolerance=±5% resistance=220 package=THT]
  1K_2 = Resistor [tolerance=±5% resistance=220 package=THT]
  1K_3 = Resistor [tolerance=±5% resistance=220 package=THT]
  motor = Screw terminal - 2 pins [package=THT]
  IN = screw terminal, 4 pins

nets:
  N1: 2N3904.E, 2N3904_2.C, 1N4007.anode, 1N4007_3.cathode, motor.pin1
  N2: 2N3904.B, 1K_2.Pin_1
  N3: 2N3904.C, 2N3904_4.C, 1N4007.cathode, 1N4007_2.cathode, IN.pin2
  N4: 2N3904_2.E, 2N3904_3.E, 1N4007_3.anode, 1N4007_4.anode, IN.pin3
  N5: 2N3904_2.B, 1K_3.Pin_1
  N6: 2N3904_3.B, 1K.Pin_0
  N7: 2N3904_3.C, 2N3904_4.E, 1N4007_2.anode, 1N4007_4.cathode, motor.pin2
  N8: 2N3904_4.B, 1k.Pin_0
  N9: 1k.Pin_1, 1K_3.Pin_0, IN.pin4
  N10: 1K.Pin_1, 1K_2.Pin_0, IN.pin1

notes:
  +
  -
  5V
  I
  D
